# Fritzing sketch BTS7960Anschluss (saved by Fritzing 1.0.6)
breadboards: 1

parts:
  A1 = Arduino UNO R4 WiFi
  M3 = DC Motor [voltage_(max)=6V voltage_(min)=3V]
  A2 = drv-1012
  R1 = Rotary Potentiometer (Small) [maximum_resistance=10kΩ knob_status=50% power=0.5W package=THT]
  V1 = DC Power Supply [voltage=12V internal_resistance=1Ω max_current=0.1A]

nets:
  N1: A1.Pin_2, A1.Pin_9, A1.Pin_30, A1.Pin_48, A2.Pin_1, A2.Pin_12, R1.leg1, V1.Pin_1
  N2: A1.Pin_8, A2.Pin_5, A2.Pin_7, R1.leg2
  N3: A1.Pin_12, R1.wiper
  N4: A1.Pin_39, A2.Pin_4
  N5: A1.Pin_40, A2.Pin_8
  N6: M3.pin_1, A2.Pin_10
  N7: M3.pin_2, A2.Pin_9
  N8: A2.Pin_11, V1.Pin_2

custom parts:
  Arduino UNO R4 WiFi: The Arduino UNO R4 WiFi merges the RA4M1 microprocessor from Renesas with the ESP32-S3 from Espressif, creating an all-in-one tool for makers with enhanced processing power and a diverse array of new peripherals.
  drv-1012: .The BTS7960 is a fully integrated high current H bridge module for motor drive applications.
