# Fritzing sketch Blink (saved by Fritzing 1.0.6)

parts:
  A1 = Arduino UNO R4 WiFi
  R1 = Resistor [tolerance=±5% power=0.25W resistance=220 package=THT]
  LED1 = LED - 5mm [color="Red (633nm)" current=0.030A package="5 mm [THT]"]

nets:
  N1: A1.Pin_47, R1.Pin_1
  N2: A1.Pin_48, LED1.cathode
  N3: R1.Pin_0, LED1.anode

custom parts:
  Arduino UNO R4 WiFi: The Arduino UNO R4 WiFi merges the RA4M1 microprocessor from Renesas with the ESP32-S3 from Espressif, creating an all-in-one tool for makers with enhanced processing power and a diverse array of new peripherals.
