# Fritzing sketch LSSimple260414 (saved by Fritzing 1.0.6)

parts:
  A1 = Arduino UNO R4 WiFi
  M1 = E18-D80NK_1 [package=THT]
  R1 = Resistor [tolerance=±5% power=0.25W resistance=100 package=THT]

nets:
  N1: A1.Pin_2, A1.Pin_9, M1.pin3
  N2: A1.Pin_42, M1.pin1, R1.Pin_1
  N3: M1.pin2, R1.Pin_0

custom parts:
  Arduino UNO R4 WiFi: The Arduino UNO R4 WiFi merges the RA4M1 microprocessor from Renesas with the ESP32-S3 from Espressif, creating an all-in-one tool for makers with enhanced processing power and a diverse array of new peripherals.
  E18-D80NK_1: E18-D80NK Proximity Sensor module.
