# Fritzing sketch regelung (saved by Fritzing 1.0.6)

parts:
  A1 = drv-1012
  A2 = Arduino UNO R4 WiFi
  Bauteil1 = FC-03
  M1 = DC Motor [voltage_(max)=6V voltage_(min)=3V]

nets:
  N1: A1.Pin_1, A2.Pin_2, A2.Pin_9, A2.Pin_10, A2.Pin_48, Bauteil1.GND
  N2: A1.Pin_4, A2.Pin_43
  N3: A1.Pin_5, A2.Pin_8, Bauteil1.VCC
  N4: A1.Pin_9, M1.pin_2
  N5: A1.Pin_10, M1.pin_1
  N6: A2.Pin_36, Bauteil1.D0

custom parts:
  drv-1012: .The BTS7960 is a fully integrated high current H bridge module for motor drive applications.
  Arduino UNO R4 WiFi: The Arduino UNO R4 WiFi merges the RA4M1 microprocessor from Renesas with the ESP32-S3 from Espressif, creating an all-in-one tool for makers with enhanced processing power and a diverse array of new peripherals.
  FC-03: FC-03, LM393 IR Speed Sensor Encoder By Nandan
